// Logisim project 4.circ as structural Verilog: 1 circuit, main circuit main
module main (
  output Q2,
  output Q1,
  output Q0
);

  wire and_1_out, and_2_out, and_3_out, and_4_out, and_5_out, clock_1_out, d_ff_1_qn, d_ff_2_qn, d_ff_3_qn,
       or_1_out, or_2_out;

  and and_1 (and_1_out, d_ff_1_qn, Q1, Q0);
  and and_2 (and_2_out, Q2, d_ff_2_qn);
  and and_3 (and_3_out, Q2, d_ff_3_qn);
  and and_4 (and_4_out, d_ff_2_qn, Q0);
  and and_5 (and_5_out, Q1, d_ff_3_qn);
  or or_1 (or_1_out, and_4_out, and_5_out);
  or or_2 (or_2_out, and_1_out, and_2_out, and_3_out);
  Clock #(.lowDuration(3)) clock_1 (.out(clock_1_out));
  D_Flip_Flop d_ff_1 (.D(or_2_out), .clk(clock_1_out), .Q(Q2), .Qn(d_ff_1_qn));  // open: preset, reset
  D_Flip_Flop d_ff_2 (.D(or_1_out), .clk(clock_1_out), .Q(Q1), .Qn(d_ff_2_qn));  // open: preset, reset
  D_Flip_Flop d_ff_3 (.D(d_ff_3_qn), .clk(clock_1_out), .Q(Q0), .Qn(d_ff_3_qn));  // open: preset, reset
endmodule
